# Fritzing sketch turntable (saved by Fritzing 0.9.1b)
breadboards: 1
stripboards: 1

parts:
  M1 = DC Motor
  D1 = Zener Diode [part_number=1N4732A breakdown_voltage=3.6V package="300 mil [THT]"]  # not connected
  R1 = Resistor [tolerance=±5% resistance=1k package=THT]
  Q1 = NPN-Transistor [package="SOT-23 [SMD]"]
  Part1 = Arduino Leonardo (Rev3b)
  J6 = Power Jack [package=power_jack_smd]
  R2 = Rotary Potentiometer (Small) [maximum_resistance=100kΩ package=THT]
  R3 = Resistor [tolerance=±5% resistance=100 package=THT]
  R4 = Resistor [tolerance=±5% resistance=160 package=THT]
  R5 = Resistor [tolerance=±5% resistance=220 package=THT]
  R6 = Resistor [tolerance=±5% resistance=330 package=THT]
  R7 = Resistor [tolerance=±5% resistance=680 package=THT]
  R8 = Resistor [tolerance=±5% resistance=470 package=THT]
  R9 = Resistor [tolerance=±5% resistance=1k package=THT]
  S1 = Square Pushbutton
  S2 = Square Pushbutton
  S3 = Square Pushbutton
  S4 = Square Pushbutton
  S5 = Square Pushbutton
  S6 = Square Pushbutton
  R10 = Rotary Potentiometer (Small) [maximum_resistance=100kΩ package=THT]
  Q2 = LTR-301 [package=ltr-301]
  LED2 = smd LED [color="Infrared (850nm)" package="0603 [SMD]"]
  R11 = Resistor [tolerance=±5% resistance=1M package=THT]
  R12 = Resistor [tolerance=±5% resistance=270 package=THT]
  Q4 = PNP-Transistor [package="TO92 [THT]"]
  D2 = Zener Diode [part_number=1N4732A breakdown_voltage=3.6V package="300 mil [THT]"]
  D3 = Zener Diode [part_number=1N4732A breakdown_voltage=3.6V package="300 mil [THT]"]
  D4 = Zener Diode [part_number=1N4732A breakdown_voltage=3.6V package="300 mil [THT]"]
  R13 = Resistor [tolerance=±5% resistance=1k package=THT]
  R15 = Resistor [tolerance=±5% resistance=100 package=THT]
  R17 = Resistor [tolerance=±5% resistance=100 package=THT]
  Q6 = NPN-Transistor [package="SOT-23 [SMD]"]
  Q7 = PNP-Transistor [package="TO92 [THT]"]
  Q8 = PNP-Transistor [package="TO92 [THT]"]  # not connected
  Q9 = PNP-Transistor [package="TO92 [THT]"]  # not connected
  Q10 = PNP-Transistor [package="TO92 [THT]"]
  D5 = Zener Diode [part_number=1N4732A breakdown_voltage=3.6V package="300 mil [THT]"]
  Q11 = NPN-Transistor [package="SOT-23 [SMD]"]
  R18 = Resistor [tolerance=±5% resistance=100 package=THT]
  D6 = Zener Diode [part_number=1N4732A breakdown_voltage=3.6V package="300 mil [THT]"]
  R19 = Resistor [tolerance=±5% resistance=1k package=THT]
  Q12 = PNP-Transistor [package="TO92 [THT]"]
  D7 = Zener Diode [part_number=1N4732A breakdown_voltage=3.6V package="300 mil [THT]"]
  D8 = Zener Diode [part_number=1N4732A breakdown_voltage=3.6V package="300 mil [THT]"]
  Q13 = NPN-Transistor [package="SOT-23 [SMD]"]
  R20 = Resistor [tolerance=±5% resistance=100 package=THT]
  R21 = Resistor [tolerance=±5% resistance=1k package=THT]

nets:
  N1: M1.pin_1, D4.cathode
  N2: M1.pin_2, D2.anode, D3.cathode
  N3: R1.Pin_0, Q1.0
  GND: Q1.2, Part1.GND, J6.GND, R2.leg1, R2.leg2, R3.Pin_1, R4.Pin_1, R5.Pin_1, R6.Pin_1, R7.Pin_1, R8.Pin_1, R9.Pin_1, R10.leg1, Q2.E, LED2.cathode, Q6.2
  N4: Q1.1, R15.Pin_0
  N5: Part1.D2/SDA, Part1.A1, R9.Pin_0, S1.leg0, S2.leg0, S3.leg0, S4.leg0, S5.leg0, S6.leg0, R10.leg2
  N6: Part1.5V, J6.PWR, R11.Pin_0, R12.Pin_0, Q4.E, Q7.E
  N7: Part1.A0, R2.wiper
  N8: Part1.A2, Q2.C, R11.Pin_1
  N9: Part1.A3, R10.wiper
  N10: R3.Pin_0, S5.leg1
  N11: R4.Pin_0, S6.leg1
  N12: R5.Pin_0, S2.leg1
  N13: R6.Pin_0, S1.leg1
  N14: R7.Pin_0, S3.leg1
  N15: R8.Pin_0, S4.leg1
  N16: LED2.anode, R12.Pin_1
  N17: Q4.B, R15.Pin_1
  N18: Q4.C, D3.anode
  N19: D2.cathode, R17.Pin_0, Q6.1
  N20: D4.anode, Q7.C
  N21: R13.Pin_0, Q6.0
  N22: R17.Pin_1, Q7.B
  N23: Q10.E, Q12.E
  N24: Q10.B, R18.Pin_1
  N25: Q10.C, D5.anode
  N26: D5.cathode, D8.anode
  N27: Q11.2, Q13.2
  N28: Q11.0, R19.Pin_0
  N29: Q11.1, R18.Pin_0, D6.cathode
  N30: D6.anode, D7.cathode
  N31: R19.Pin_1, R21.Pin_1
  N32: Q12.C, D7.anode
  N33: D8.cathode, Q13.1, R20.Pin_0
  N34: Q13.0, R21.Pin_0
